// Logisim project main.circ as structural Verilog: 2 circuits, main circuit main
module front (
);

  wire clock_1_out, L_out, R_out, RST_out;
  wire [3:0] main_1_d0, main_1_d1, main_1_d2, main_1_d3, main_1_d4, main_1_d5, main_1_d6, main_1_d7;
  wire [31:0] main_1__0, main_1__1, main_1__2, main_1__3, main_1__4, main_1__5, main_1__6, main_1__7,
       main_1__8, main_1__9, main_1__10, main_1__11, main_1__12, main_1__13, main_1__14, main_1__15,
       main_1__16, main_1__17, main_1__18, main_1__19, main_1__20, main_1__21, main_1__22, main_1__23,
       main_1__24, main_1__25, main_1__26, main_1__27, main_1__28, main_1__29, main_1__30, main_1__31;

  Hex_Digit_Display hex_digit_display_1 (.value(main_1_d7));  // open: dp
  main main_1 (
    ._0(main_1__0), ._1(main_1__1), ._2(main_1__2), ._3(main_1__3), ._4(main_1__4), ._5(main_1__5),
    ._6(main_1__6), ._7(main_1__7), ._8(main_1__8), ._9(main_1__9), ._10(main_1__10), ._11(main_1__11),
    ._12(main_1__12), ._13(main_1__13), ._31(main_1__31), ._14(main_1__14), ._15(main_1__15),
    ._16(main_1__16), ._17(main_1__17), ._18(main_1__18), ._19(main_1__19), ._20(main_1__20),
    ._21(main_1__21), ._22(main_1__22), ._23(main_1__23), ._24(main_1__24), ._25(main_1__25),
    ._26(main_1__26), ._27(main_1__27), ._28(main_1__28), ._29(main_1__29), ._30(main_1__30), .D0(main_1_d0),
    .D1(main_1_d1), .D2(main_1_d2), .D3(main_1_d3), .D4(main_1_d4), .D5(main_1_d5), .D6(main_1_d6),
    .D7(main_1_d7), .R(R_out), .L(L_out), .CLK(clock_1_out), .RST(RST_out));
  Clock clock_1 (.out(clock_1_out));
  Hex_Digit_Display hex_digit_display_2 (.value(main_1_d6));  // open: dp
  DotMatrix #(.inputtype("row"), .matrixcols(32), .matrixrows(32)) dotmatrix_1 (
    .row0(main_1__0), .row1(main_1__1), .row2(main_1__2), .row3(main_1__3), .row4(main_1__4),
    .row5(main_1__5), .row6(main_1__6), .row7(main_1__7), .row8(main_1__8), .row9(main_1__9),
    .row10(main_1__10), .row11(main_1__11), .row12(main_1__12), .row13(main_1__13), .row14(main_1__14),
    .row15(main_1__15), .row16(main_1__16), .row17(main_1__17), .row18(main_1__18), .row19(main_1__19),
    .row20(main_1__20), .row21(main_1__21), .row22(main_1__22), .row23(main_1__23), .row24(main_1__24),
    .row25(main_1__25), .row26(main_1__26), .row27(main_1__27), .row28(main_1__28), .row29(main_1__29),
    .row30(main_1__30), .row31(main_1__31));
  Button RST (.out(RST_out));
  Hex_Digit_Display hex_digit_display_3 (.value(main_1_d4));  // open: dp
  Hex_Digit_Display hex_digit_display_4 (.value(main_1_d5));  // open: dp
  Button L (.out(L_out));
  Hex_Digit_Display hex_digit_display_5 (.value(main_1_d3));  // open: dp
  Hex_Digit_Display hex_digit_display_6 (.value(main_1_d2));  // open: dp
  Button R (.out(R_out));
  Hex_Digit_Display hex_digit_display_7 (.value(main_1_d1));  // open: dp
  Hex_Digit_Display hex_digit_display_8 (.value(main_1_d0));  // open: dp

  // Notes on the sheet:
  //   hp
endmodule

module main (
  input  R,
  input  L,
  input  CLK,
  input  RST,
  output [31:0] _0,
  output [31:0] _1,
  output [31:0] _2,
  output [31:0] _3,
  output [31:0] _4,
  output [31:0] _5,
  output [31:0] _6,
  output [31:0] _7,
  output [31:0] _8,
  output [31:0] _9,
  output [31:0] _10,
  output [31:0] _11,
  output [31:0] _12,
  output [31:0] _13,
  output [31:0] _14,
  output [31:0] _15,
  output [31:0] _16,
  output [31:0] _17,
  output [31:0] _18,
  output [31:0] _19,
  output [31:0] _20,
  output [31:0] _21,
  output [31:0] _22,
  output [31:0] _23,
  output [31:0] _24,
  output [31:0] _25,
  output [31:0] _26,
  output [31:0] _27,
  output [31:0] _28,
  output [31:0] _29,
  output [31:0] _30,
  output [31:0] _31,
  output [3:0] D0,
  output [3:0] D1,
  output [3:0] D2,
  output [3:0] D3,
  output [3:0] D4,
  output [3:0] D5,
  output [3:0] D6,
  output [3:0] D7
);

  wire and_5_out, and_6_out, CLK_t, COL1, COL2, comparator_1_lt, comparator_2_gt, comparator_3_gt,
       comparator_4_gt, comparator_6_gt, comparator_7_lt, comparator_8_gt, comparator_9_gt, comparator_10_gt,
       comparator_11_gt, counter_1_carry, counter_2_carry, counter_3_carry, counter_5_carry, counter_7_carry,
       counter_8_carry, counter_10_carry, demultiplexer_1_out0, demultiplexer_1_out1, HA, multiplexer_1_out,
       not_1_out, not_2_out, not_3_out, or_1_out, or_34_out, or_35_out, or_40_out, or_41_out, or_42_out,
       or_43_out;
  wire [4:0] counter_11_q, random_1_out, random_2_out;
  wire [31:0] adder_1_out, and_1_out, and_2_out, and_3_out, and_4_out, and_7_out, and_8_out, and_9_out,
       and_10_out, B0, B1, B2, B3, B4, B5, B6, B7, B8, B9, B10, B11, B12, B13, B14, B15, B16, B17, B18, B19,
       B20, B21, B22, B23, B24, B25, B26, B27, B28, B29, B30, B31, counter_4_q, counter_6_q, counter_9_q,
       divider_1_out, divider_1_rem, divider_2_out, divider_2_rem, divider_3_out, divider_3_rem,
       divider_4_out, divider_4_rem, divider_5_out, divider_5_rem, divider_6_out, divider_6_rem,
       multiplexer_35_out, multiplexer_36_out, multiplexer_37_out, multiplexer_38_out, multiplier_1_out, O0,
       O1, O2, O3, O4, O5, O6, O7, O8, O9, O10, O11, O12, O13, O14, O15, O16, O17, O18, O19, O20, O21, O22,
       O23, O24, O25, O26, O27, O28, O29, O30, O31, or_2_out, or_3_out, or_4_out, or_5_out, or_6_out,
       or_7_out, or_8_out, or_9_out, or_10_out, or_11_out, or_12_out, or_13_out, or_14_out, or_15_out,
       or_16_out, or_17_out, or_18_out, or_19_out, or_20_out, or_21_out, or_22_out, or_23_out, or_24_out,
       or_25_out, or_26_out, or_27_out, or_28_out, or_29_out, or_30_out, or_31_out, or_32_out, or_33_out,
       or_36_out, or_37_out, P0, P1, P2, P3, register_3_q, register_8_q, register_12_q, shifter_1_out,
       shifter_2_out, shifter_3_out, shifter_4_out, subtractor_1_out;

  assign and_1_out = P0 & O28;  // AND_Gate and_1, 32 bits wide
  Counter #(.width(32), .max('h9), .trigger("falling")) counter_1 (
    .carry(counter_1_carry), .clk(CLK_t), .clr(not_1_out));  // open: load, D, count, Q
  not not_1 (not_1_out, or_1_out);
  Counter #(.width(32), .max('h18), .trigger("falling")) counter_2 (
    .carry(counter_2_carry), .clk(counter_3_carry));  // open: load, D, count, Q, clr
  Counter #(.width(32), .max('h10), .trigger("falling")) counter_3 (
    .carry(counter_3_carry), .clk(CLK_t));  // open: load, D, count, Q, clr
  assign and_2_out = P0 & B28;  // AND_Gate and_2, 32 bits wide
  Counter #(.width(32), .max('hffffffff), .ongoal("stay"), .trigger("falling")) counter_4 (
    .Q(counter_4_q), .clk(COL1), .clr(RST));  // open: load, D, count, carry
  Counter #(.width(32), .max('h8), .trigger("falling")) counter_5 (
    .carry(counter_5_carry), .clk(CLK_t));  // open: load, D, count, Q, clr
  Counter #(.width(32), .max('hffffffff), .ongoal("stay"), .trigger("falling")) counter_6 (
    .Q(counter_6_q), .clk(COL2), .clr(RST));  // open: load, D, count, carry
  Random #(.width(5), .seed(1), .trigger("falling")) random_1 (
    .clk(counter_2_carry), .out(random_1_out));  // open: next, clr
  Counter #(.width(32), .max('h7f), .trigger("falling")) counter_7 (
    .carry(counter_7_carry), .clk(CLK_t), .clr(RST));  // open: load, D, count, Q
  Counter #(.width(32), .max('h10), .trigger("falling")) counter_8 (
    .carry(counter_8_carry), .clk(CLK_t));  // open: load, D, count, Q, clr
  Multiplexer #(.enable("false")) multiplexer_1 (
    .in0(counter_8_carry), .in1(counter_5_carry), .out(multiplexer_1_out), .sel(not_2_out));
  Comparator #(.width(4), .mode("unsigned")) comparator_1 (.a(D3), .b(4'b0001), .lt(comparator_1_lt));  // open: gt, eq
  Comparator #(.width(32), .mode("unsigned")) comparator_2 (
    .a(and_1_out), .b({32{1'b0}}), .gt(comparator_2_gt));  // open: eq, lt
  or or_1 (or_1_out, R, L);
  assign or_2_out = B0 | O0;  // OR_Gate or_2, 32 bits wide
  Multiplexer #(.width(32), .enable("false")) multiplexer_2 (.in0(or_2_out), .in1(32'h7bdfdc0), .out(_0), .sel(HA));
  assign or_3_out = B1 | O1;  // OR_Gate or_3, 32 bits wide
  Multiplexer #(.width(32), .enable("false")) multiplexer_3 (.in0(or_3_out), .in1(32'h4252500), .out(_1), .sel(HA));
  assign or_4_out = B2 | O2;  // OR_Gate or_4, 32 bits wide
  Multiplexer #(.width(32), .enable("false")) multiplexer_4 (.in0(or_4_out), .in1(32'h4252500), .out(_2), .sel(HA));
  assign or_5_out = B3 | O3;  // OR_Gate or_5, 32 bits wide
  Multiplexer #(.width(32), .enable("false")) multiplexer_5 (.in0(or_5_out), .in1(32'h5bd25c0), .out(_3), .sel(HA));
  assign or_6_out = B4 | O4;  // OR_Gate or_6, 32 bits wide
  Multiplexer #(.width(32), .enable("false")) multiplexer_6 (.in0(or_6_out), .in1(32'h4a52500), .out(_4), .sel(HA));
  assign or_7_out = B5 | O5;  // OR_Gate or_7, 32 bits wide
  Multiplexer #(.width(32), .enable("false")) multiplexer_7 (.in0(or_7_out), .in1(32'h4a52500), .out(_5), .sel(HA));
  assign or_8_out = B6 | O6;  // OR_Gate or_8, 32 bits wide
  Multiplexer #(.width(32), .enable("false")) multiplexer_8 (.in0(or_8_out), .in1(32'h7a525c0), .out(_6), .sel(HA));
  assign or_9_out = B7 | O7;  // OR_Gate or_9, 32 bits wide
  Multiplexer #(.width(32), .enable("false")) multiplexer_9 (.in0(or_9_out), .in1({32{1'b0}}), .out(_7), .sel(HA));
  assign or_10_out = B8 | O8;  // OR_Gate or_10, 32 bits wide
  Multiplexer #(.width(32), .enable("false")) multiplexer_10 (.in0(or_10_out), .in1(32'h3d17780), .out(_8), .sel(HA));
  assign or_11_out = B9 | O9;  // OR_Gate or_11, 32 bits wide
  Multiplexer #(.width(32), .enable("false")) multiplexer_11 (.in0(or_11_out), .in1(32'h2514480), .out(_9), .sel(HA));
  assign or_12_out = B10 | O10;  // OR_Gate or_12, 32 bits wide
  Multiplexer #(.width(32), .enable("false")) multiplexer_12 (.in0(or_12_out), .in1(32'h2514480), .out(_10), .sel(HA));
  assign or_13_out = B11 | O11;  // OR_Gate or_13, 32 bits wide
  Multiplexer #(.width(32), .enable("false")) multiplexer_13 (.in0(or_13_out), .in1(32'h24a7780), .out(_11), .sel(HA));
  assign or_14_out = B12 | O12;  // OR_Gate or_14, 32 bits wide
  Multiplexer #(.width(32), .enable("false")) multiplexer_14 (.in0(or_14_out), .in1(32'h24a4600), .out(_12), .sel(HA));
  assign or_15_out = B13 | O13;  // OR_Gate or_15, 32 bits wide
  Multiplexer #(.width(32), .enable("false")) multiplexer_15 (.in0(or_15_out), .in1(32'h24a4500), .out(_13), .sel(HA));
  assign or_16_out = B14 | O14;  // OR_Gate or_16, 32 bits wide
  Multiplexer #(.width(32), .enable("false")) multiplexer_16 (.in0(or_16_out), .in1(32'h3ce7480), .out(_14), .sel(HA));
  assign or_17_out = B15 | O15;  // OR_Gate or_17, 32 bits wide
  Multiplexer #(.width(32), .enable("false")) multiplexer_17 (.in0(or_17_out), .in1({32{1'b0}}), .out(_15), .sel(HA));
  assign or_18_out = B16 | O16;  // OR_Gate or_18, 32 bits wide
  Multiplexer #(.width(32), .enable("false")) multiplexer_18 (.in0(or_18_out), .in1({32{1'b0}}), .out(_16), .sel(HA));
  assign or_19_out = B17 | O17;  // OR_Gate or_19, 32 bits wide
  Multiplexer #(.width(32), .enable("false")) multiplexer_19 (.in0(or_19_out), .in1({32{1'b0}}), .out(_17), .sel(HA));
  assign or_20_out = B18 | O18;  // OR_Gate or_20, 32 bits wide
  Multiplexer #(.width(32), .enable("false")) multiplexer_20 (.in0(or_20_out), .in1({32{1'b0}}), .out(_18), .sel(HA));
  assign or_21_out = B19 | O19;  // OR_Gate or_21, 32 bits wide
  Multiplexer #(.width(32), .enable("false")) multiplexer_21 (.in0(or_21_out), .in1({32{1'b0}}), .out(_19), .sel(HA));
  assign or_22_out = B20 | O20;  // OR_Gate or_22, 32 bits wide
  Multiplexer #(.width(32), .enable("false")) multiplexer_22 (.in0(or_22_out), .in1({32{1'b0}}), .out(_20), .sel(HA));
  assign or_23_out = B21 | O21;  // OR_Gate or_23, 32 bits wide
  Multiplexer #(.width(32), .enable("false")) multiplexer_23 (.in0(or_23_out), .in1({32{1'b0}}), .out(_21), .sel(HA));
  assign or_24_out = B22 | O22;  // OR_Gate or_24, 32 bits wide
  Multiplexer #(.width(32), .enable("false")) multiplexer_24 (.in0(or_24_out), .in1({32{1'b0}}), .out(_22), .sel(HA));
  assign or_25_out = B23 | O23;  // OR_Gate or_25, 32 bits wide
  Multiplexer #(.width(32), .enable("false")) multiplexer_25 (.in0(or_25_out), .in1({32{1'b0}}), .out(_23), .sel(HA));
  assign or_26_out = B24 | O24;  // OR_Gate or_26, 32 bits wide
  Multiplexer #(.width(32), .enable("false")) multiplexer_26 (.in0(or_26_out), .in1({32{1'b0}}), .out(_24), .sel(HA));
  assign or_27_out = B25 | O25;  // OR_Gate or_27, 32 bits wide
  Multiplexer #(.width(32), .enable("false")) multiplexer_27 (.in0(or_27_out), .in1({32{1'b0}}), .out(_25), .sel(HA));
  assign or_28_out = B26 | O26;  // OR_Gate or_28, 32 bits wide
  Multiplexer #(.width(32), .enable("false")) multiplexer_28 (.in0(or_28_out), .in1({32{1'b0}}), .out(_26), .sel(HA));
  assign or_29_out = B27 | O27;  // OR_Gate or_29, 32 bits wide
  Multiplexer #(.width(32), .enable("false")) multiplexer_29 (.in0(or_29_out), .in1({32{1'b0}}), .out(_27), .sel(HA));
  assign or_30_out = B28 | P0 | O28;  // OR_Gate or_30, 32 bits wide
  Multiplexer #(.width(32), .enable("false")) multiplexer_30 (.in0(or_30_out), .in1({32{1'b0}}), .out(_28), .sel(HA));
  assign or_31_out = B29 | P1 | O29;  // OR_Gate or_31, 32 bits wide
  Multiplexer #(.width(32), .enable("false")) multiplexer_31 (.in0(or_31_out), .in1({32{1'b0}}), .out(_29), .sel(HA));
  assign or_32_out = B30 | P2 | O30;  // OR_Gate or_32, 32 bits wide
  Multiplexer #(.width(32), .enable("false")) multiplexer_32 (.in0(or_32_out), .in1({32{1'b0}}), .out(_30), .sel(HA));
  assign or_33_out = B31 | P3 | O31;  // OR_Gate or_33, 32 bits wide
  Multiplexer #(.width(32), .enable("false")) multiplexer_33 (.in0(or_33_out), .in1({32{1'b0}}), .out(_31), .sel(HA));
  Multiplexer #(.enable("false")) multiplexer_34 (.in0(CLK), .in1(1'b0), .out(CLK_t), .sel(HA));
  Multiplexer #(.width(32), .enable("false")) multiplexer_35 (
    .in0({32{1'b0}}), .in1(32'h1), .out(multiplexer_35_out), .sel(counter_2_carry));
  Comparator #(.width(32), .mode("unsigned")) comparator_3 (
    .a(and_2_out), .b({32{1'b0}}), .gt(comparator_3_gt));  // open: eq, lt
  Multiplier #(.width(32)) multiplier_1 (.a(32'h64), .b(counter_4_q), .out(multiplier_1_out));  // open: cin, cout
  Counter #(.width(32), .max('hffffffff), .ongoal("stay"), .trigger("falling")) counter_9 (
    .Q(counter_9_q), .clk(counter_7_carry), .clr(RST));  // open: load, D, count, carry
  Counter #(.width(32), .max('h2), .trigger("falling")) counter_10 (
    .carry(counter_10_carry), .clk(multiplexer_1_out));  // open: load, D, count, Q, clr
  not not_2 (not_2_out, comparator_1_lt);
  assign and_3_out = P1 & O29;  // AND_Gate and_3, 32 bits wide
  Bit_Extender #(.in_width(32), .out_width(4)) bit_extender_1 (.in(subtractor_1_out), .out(D7));
  Subtractor #(.width(32)) subtractor_1 (.a(32'h5), .b(counter_6_q), .out(subtractor_1_out));  // open: bin, bout
  Register #(.width(32), .trigger("falling")) register_1 (
    .D(shifter_1_out), .Q(B0), .clk(counter_3_carry), .clr(RST));  // open: en
  Shifter #(.width(32)) shifter_1 (.in(multiplexer_35_out), .\dist (random_1_out), .out(shifter_1_out));
  assign and_4_out = P1 & B29;  // AND_Gate and_4, 32 bits wide
  Adder #(.width(32)) adder_1 (.a(multiplier_1_out), .b(counter_9_q), .out(adder_1_out));  // open: cin, cout
  Multiplexer #(.width(32), .enable("false")) multiplexer_36 (
    .in0({32{1'b0}}), .in1(32'h2), .out(multiplexer_36_out), .sel(and_6_out));
  Shifter #(.width(32)) shifter_2 (.in(multiplexer_36_out), .\dist (random_2_out), .out(shifter_2_out));
  Comparator #(.width(32), .mode("unsigned")) comparator_4 (
    .a(and_3_out), .b({32{1'b0}}), .gt(comparator_4_gt));  // open: eq, lt
  Comparator #(.width(32), .mode("unsigned")) comparator_5 (
    .a(subtractor_1_out), .b({32{1'b0}}), .eq(HA));  // open: gt, lt
  and and_5 (and_5_out, ~counter_1_carry, ~HA, or_1_out);  // AND_Gate
  Demultiplexer #(.enable("false")) demultiplexer_1 (
    .out0(demultiplexer_1_out0), .out1(demultiplexer_1_out1), .in(and_5_out), .sel(L));
  Register #(.width(32), .trigger("falling")) register_2 (
    .D(B0), .Q(B1), .clk(counter_3_carry), .clr(RST));  // open: en
  Comparator #(.width(32), .mode("unsigned")) comparator_6 (
    .a(and_4_out), .b({32{1'b0}}), .gt(comparator_6_gt));  // open: eq, lt
  Divider #(.width(32)) divider_1 (
    .a(adder_1_out), .b(32'hf4240), .out(divider_1_out), .rem(divider_1_rem));  // open: upper
  Random #(.width(5), .seed(2), .trigger("falling")) random_2 (
    .clk(counter_10_carry), .out(random_2_out));  // open: next, clr
  and and_6 (and_6_out, counter_10_carry, comparator_7_lt);
  Register #(.width(32), .trigger("falling")) register_3 (
    .D(shifter_2_out), .Q(register_3_q), .clk(multiplexer_1_out), .clr(or_34_out));  // open: en
  or or_34 (or_34_out, COL2, RST);
  assign and_7_out = P2 & O30;  // AND_Gate and_7, 32 bits wide
  or or_35 (or_35_out, demultiplexer_1_out0, demultiplexer_1_out1);
  not not_3 (not_3_out, or_35_out);
  Register #(.width(32), .trigger("falling")) register_4 (
    .D(B2), .Q(B3), .clk(counter_3_carry), .clr(RST));  // open: en
  Register #(.width(32), .trigger("falling")) register_5 (
    .D(B1), .Q(B2), .clk(counter_3_carry), .clr(RST));  // open: en
  assign and_8_out = P2 & B30;  // AND_Gate and_8, 32 bits wide
  Bit_Extender #(.in_width(32), .out_width(4)) bit_extender_2 (.in(divider_1_out), .out(D6));
  Bit_Extender #(.in_width(32), .out_width(4)) bit_extender_3 (.in(divider_2_out), .out(D5));
  Divider #(.width(32)) divider_2 (
    .a(divider_1_rem), .b(32'h186a0), .out(divider_2_out), .rem(divider_2_rem));  // open: upper
  Divider #(.width(32)) divider_3 (
    .a(divider_2_rem), .b(32'h2710), .out(divider_3_out), .rem(divider_3_rem));  // open: upper
  Comparator #(.width(5), .mode("unsigned")) comparator_7 (
    .a(random_2_out), .b(5'b11110), .lt(comparator_7_lt));  // open: gt, eq
  Multiplexer #(.width(32), .enable("false")) multiplexer_37 (
    .in0({32{1'b0}}), .in1(32'h5), .out(multiplexer_37_out), .sel(and_6_out));
  Shifter #(.width(32)) shifter_3 (.in(multiplexer_37_out), .\dist (random_2_out), .out(shifter_3_out));
  Counter #(.width(5), .max('h1d), .ongoal("stay"), .trigger("falling")) counter_11 (
    .load(demultiplexer_1_out0), .Q(counter_11_q), .clk(not_3_out), .clr(RST));  // open: D, count, carry
  Register #(.width(32), .trigger("falling")) register_6 (
    .D(B3), .Q(B4), .clk(counter_3_carry), .clr(RST));  // open: en
  Register #(.width(32), .trigger("falling")) register_7 (
    .D(B4), .Q(B5), .clk(counter_3_carry), .clr(RST));  // open: en
  Bit_Extender #(.in_width(32), .out_width(4)) bit_extender_4 (.in(divider_3_out), .out(D4));
  Bit_Extender #(.in_width(32), .out_width(4)) bit_extender_5 (.in(divider_4_out), .out(D3));
  Divider #(.width(32)) divider_4 (
    .a(divider_3_rem), .b(32'h3e8), .out(divider_4_out), .rem(divider_4_rem));  // open: upper
  Divider #(.width(32)) divider_5 (
    .a(divider_4_rem), .b(32'h64), .out(divider_5_out), .rem(divider_5_rem));  // open: upper
  assign or_36_out = shifter_3_out | register_3_q;  // OR_Gate or_36, 32 bits wide
  Register #(.width(32), .trigger("falling")) register_8 (
    .D(or_36_out), .Q(register_8_q), .clk(multiplexer_1_out), .clr(or_34_out));  // open: en
  Comparator #(.width(32), .mode("unsigned")) comparator_8 (
    .a(and_7_out), .b({32{1'b0}}), .gt(comparator_8_gt));  // open: eq, lt
  Register #(.width(32), .trigger("falling")) register_9 (
    .D(B5), .Q(B6), .clk(counter_3_carry), .clr(RST));  // open: en
  Comparator #(.width(32), .mode("unsigned")) comparator_9 (
    .a(and_8_out), .b({32{1'b0}}), .gt(comparator_9_gt));  // open: eq, lt
  assign and_9_out = P3 & B31;  // AND_Gate and_9, 32 bits wide
  Bit_Extender #(.in_width(32), .out_width(4)) bit_extender_6 (.in(divider_5_out), .out(D2));
  Bit_Extender #(.in_width(32), .out_width(4)) bit_extender_7 (.in(divider_6_out), .out(D1));
  Divider #(.width(32)) divider_6 (
    .a(divider_5_rem), .b(32'ha), .out(divider_6_out), .rem(divider_6_rem));  // open: upper
  Bit_Extender #(.in_width(32), .out_width(4)) bit_extender_8 (.in(divider_6_rem), .out(D0));
  Multiplexer #(.width(32), .enable("false")) multiplexer_38 (
    .in0({32{1'b0}}), .in1(32'h2), .out(multiplexer_38_out), .sel(and_6_out));
  Shifter #(.width(32)) shifter_4 (.in(multiplexer_38_out), .\dist (random_2_out), .out(shifter_4_out));
  assign and_10_out = P3 & O31;  // AND_Gate and_10, 32 bits wide
  Shifter #(.width(32)) shifter_5 (.in(32'h2), .\dist (counter_11_q), .out(P0));
  Shifter #(.width(32)) shifter_6 (.in(32'h7), .\dist (counter_11_q), .out(P1));
  Shifter #(.width(32)) shifter_7 (.in(32'h2), .\dist (counter_11_q), .out(P2));
  Shifter #(.width(32)) shifter_8 (.in(32'h7), .\dist (counter_11_q), .out(P3));
  Register #(.width(32), .trigger("falling")) register_10 (
    .D(B6), .Q(B7), .clk(counter_3_carry), .clr(RST));  // open: en
  Register #(.width(32), .trigger("falling")) register_11 (
    .D(B7), .Q(B8), .clk(counter_3_carry), .clr(RST));  // open: en
  Register #(.width(32), .trigger("falling")) register_12 (
    .D(or_37_out), .Q(register_12_q), .clk(multiplexer_1_out), .clr(or_34_out));  // open: en
  assign or_37_out = shifter_4_out | register_8_q;  // OR_Gate or_37, 32 bits wide
  Comparator #(.width(32), .mode("unsigned")) comparator_10 (
    .a(and_10_out), .b({32{1'b0}}), .gt(comparator_10_gt));  // open: eq, lt
  Register #(.width(32), .trigger("falling")) register_13 (
    .D(B8), .Q(B9), .clk(counter_3_carry), .clr(RST));  // open: en
  Comparator #(.width(32), .mode("unsigned")) comparator_11 (
    .a(and_9_out), .b({32{1'b0}}), .gt(comparator_11_gt));  // open: eq, lt
  Register #(.width(32), .trigger("falling")) register_14 (
    .D(register_12_q), .Q(O0), .clk(multiplexer_1_out), .clr(or_34_out));  // open: en
  or or_38 (COL2, comparator_10_gt, comparator_8_gt, comparator_4_gt, comparator_2_gt);
  Register #(.width(32), .trigger("falling")) register_15 (
    .D(B9), .Q(B10), .clk(counter_3_carry), .clr(RST));  // open: en
  Register #(.width(32), .trigger("falling")) register_16 (
    .D(B10), .Q(B11), .clk(counter_3_carry), .clr(RST));  // open: en
  or or_39 (COL1, comparator_11_gt, comparator_9_gt, comparator_6_gt, comparator_3_gt);
  Register #(.width(32), .trigger("falling")) register_17 (
    .D(O1), .Q(O2), .clk(multiplexer_1_out), .clr(or_34_out));  // open: en
  Register #(.width(32), .trigger("falling")) register_18 (
    .D(O0), .Q(O1), .clk(multiplexer_1_out), .clr(or_34_out));  // open: en
  Register #(.width(32), .trigger("falling")) register_19 (
    .D(B12), .Q(B13), .clk(counter_3_carry), .clr(RST));  // open: en
  Register #(.width(32), .trigger("falling")) register_20 (
    .D(B11), .Q(B12), .clk(counter_3_carry), .clr(RST));  // open: en
  Register #(.width(32), .trigger("falling")) register_21 (
    .D(O2), .Q(O3), .clk(multiplexer_1_out), .clr(or_34_out));  // open: en
  Register #(.width(32), .trigger("falling")) register_22 (
    .D(B13), .Q(B14), .clk(counter_3_carry), .clr(RST));  // open: en
  Register #(.width(32), .trigger("falling")) register_23 (
    .D(O4), .Q(O5), .clk(multiplexer_1_out), .clr(or_34_out));  // open: en
  Register #(.width(32), .trigger("falling")) register_24 (
    .D(O3), .Q(O4), .clk(multiplexer_1_out), .clr(or_34_out));  // open: en
  Register #(.width(32), .trigger("falling")) register_25 (
    .D(B14), .Q(B15), .clk(counter_3_carry), .clr(RST));  // open: en
  Register #(.width(32), .trigger("falling")) register_26 (
    .D(B15), .Q(B16), .clk(counter_3_carry), .clr(RST));  // open: en
  Register #(.width(32), .trigger("falling")) register_27 (
    .D(O5), .Q(O6), .clk(multiplexer_1_out), .clr(or_34_out));  // open: en
  Register #(.width(32), .trigger("falling")) register_28 (
    .D(O6), .Q(O7), .clk(multiplexer_1_out), .clr(or_34_out));  // open: en
  Register #(.width(32), .trigger("falling")) register_29 (
    .D(B16), .Q(B17), .clk(counter_3_carry), .clr(RST));  // open: en
  Register #(.width(32), .trigger("falling")) register_30 (
    .D(O7), .Q(O8), .clk(multiplexer_1_out), .clr(or_34_out));  // open: en
  Register #(.width(32), .trigger("falling")) register_31 (
    .D(B18), .Q(B19), .clk(counter_3_carry), .clr(RST));  // open: en
  Register #(.width(32), .trigger("falling")) register_32 (
    .D(B17), .Q(B18), .clk(counter_3_carry), .clr(RST));  // open: en
  Register #(.width(32), .trigger("falling")) register_33 (
    .D(O8), .Q(O9), .clk(multiplexer_1_out), .clr(or_34_out));  // open: en
  Register #(.width(32), .trigger("falling")) register_34 (
    .D(O9), .Q(O10), .clk(multiplexer_1_out), .clr(or_34_out));  // open: en
  Register #(.width(32), .trigger("falling")) register_35 (
    .D(B20), .Q(B21), .clk(counter_3_carry), .clr(RST));  // open: en
  Register #(.width(32), .trigger("falling")) register_36 (
    .D(B19), .Q(B20), .clk(counter_3_carry), .clr(RST));  // open: en
  Register #(.width(32), .trigger("falling")) register_37 (
    .D(O10), .Q(O11), .clk(multiplexer_1_out), .clr(or_34_out));  // open: en
  Register #(.width(32), .trigger("falling")) register_38 (
    .D(B21), .Q(B22), .clk(counter_3_carry), .clr(RST));  // open: en
  Register #(.width(32), .trigger("falling")) register_39 (
    .D(O11), .Q(O12), .clk(multiplexer_1_out), .clr(or_34_out));  // open: en
  Register #(.width(32), .trigger("falling")) register_40 (
    .D(O12), .Q(O13), .clk(multiplexer_1_out), .clr(or_34_out));  // open: en
  Register #(.width(32), .trigger("falling")) register_41 (
    .D(B22), .Q(B23), .clk(counter_3_carry), .clr(RST));  // open: en
  Register #(.width(32), .trigger("falling")) register_42 (
    .D(B23), .Q(B24), .clk(counter_3_carry), .clr(RST));  // open: en
  Register #(.width(32), .trigger("falling")) register_43 (
    .D(O13), .Q(O14), .clk(multiplexer_1_out), .clr(or_34_out));  // open: en
  Register #(.width(32), .trigger("falling")) register_44 (
    .D(O14), .Q(O15), .clk(multiplexer_1_out), .clr(or_34_out));  // open: en
  Register #(.width(32), .trigger("falling")) register_45 (
    .D(B24), .Q(B25), .clk(counter_3_carry), .clr(RST));  // open: en
  Register #(.width(32), .trigger("falling")) register_46 (
    .D(O15), .Q(O16), .clk(multiplexer_1_out), .clr(or_34_out));  // open: en
  Register #(.width(32), .trigger("falling")) register_47 (
    .D(B25), .Q(B26), .clk(counter_3_carry), .clr(RST));  // open: en
  Register #(.width(32), .trigger("falling")) register_48 (
    .D(B26), .Q(B27), .clk(counter_3_carry), .clr(RST));  // open: en
  Register #(.width(32), .trigger("falling")) register_49 (
    .D(O16), .Q(O17), .clk(multiplexer_1_out), .clr(or_34_out));  // open: en
  Register #(.width(32), .trigger("falling")) register_50 (
    .D(O17), .Q(O18), .clk(multiplexer_1_out), .clr(or_34_out));  // open: en
  Register #(.width(32), .trigger("falling")) register_51 (
    .D(B27), .Q(B28), .clk(counter_3_carry), .clr(or_40_out));  // open: en
  Register #(.width(32), .trigger("falling")) register_52 (
    .D(B28), .Q(B29), .clk(counter_3_carry), .clr(or_41_out));  // open: en
  or or_40 (or_40_out, COL1, RST);
  or or_41 (or_41_out, COL1, RST);
  Register #(.width(32), .trigger("falling")) register_53 (
    .D(O18), .Q(O19), .clk(multiplexer_1_out), .clr(or_34_out));  // open: en
  Register #(.width(32), .trigger("falling")) register_54 (
    .D(B29), .Q(B30), .clk(counter_3_carry), .clr(or_42_out));  // open: en
  or or_42 (or_42_out, COL1, RST);
  Register #(.width(32), .trigger("falling")) register_55 (
    .D(O19), .Q(O20), .clk(multiplexer_1_out), .clr(or_34_out));  // open: en
  Register #(.width(32), .trigger("falling")) register_56 (
    .D(O20), .Q(O21), .clk(multiplexer_1_out), .clr(or_34_out));  // open: en
  Register #(.width(32), .trigger("falling")) register_57 (
    .D(B30), .Q(B31), .clk(counter_3_carry), .clr(or_43_out));  // open: en
  or or_43 (or_43_out, COL1, RST);
  Register #(.width(32), .trigger("falling")) register_58 (
    .D(O22), .Q(O23), .clk(multiplexer_1_out), .clr(or_34_out));  // open: en
  Register #(.width(32), .trigger("falling")) register_59 (
    .D(O21), .Q(O22), .clk(multiplexer_1_out), .clr(or_34_out));  // open: en
  Register #(.width(32), .trigger("falling")) register_60 (
    .D(O23), .Q(O24), .clk(multiplexer_1_out), .clr(or_34_out));  // open: en
  Register #(.width(32), .trigger("falling")) register_61 (
    .D(O24), .Q(O25), .clk(multiplexer_1_out), .clr(or_34_out));  // open: en
  Register #(.width(32), .trigger("falling")) register_62 (
    .D(O25), .Q(O26), .clk(multiplexer_1_out), .clr(or_34_out));  // open: en
  Register #(.width(32), .trigger("falling")) register_63 (
    .D(O26), .Q(O27), .clk(multiplexer_1_out), .clr(or_34_out));  // open: en
  Register #(.width(32), .trigger("falling")) register_64 (
    .D(O28), .Q(O29), .clk(multiplexer_1_out), .clr(or_34_out));  // open: en
  Register #(.width(32), .trigger("falling")) register_65 (
    .D(O27), .Q(O28), .clk(multiplexer_1_out), .clr(or_34_out));  // open: en
  Register #(.width(32), .trigger("falling")) register_66 (
    .D(O29), .Q(O30), .clk(multiplexer_1_out), .clr(or_34_out));  // open: en
  Register #(.width(32), .trigger("falling")) register_67 (
    .D(O30), .Q(O31), .clk(multiplexer_1_out), .clr(or_34_out));  // open: en

  // Notes on the sheet:
  //   points
  //   display
  //   input
  //   bonus
  //   collision bonus
  //   obstacle
  //   collision obstacle
  //   hp
  //   player
  //   segment display
  //   halt
endmodule
